# Fritzing sketch WC timer V1.0 (saved by Fritzing 0.9.2b)
circuit board: 6.40438cm x 4.96368cm
breadboards: 1

parts:
  R1 = Resistor [tolerance=±5% resistance=220 package=THT]
  R2 = Trimmer Potentiometer [maximum_resistance=10kΩ package=THT]
  R3 = Resistor [tolerance=±5% resistance=2.2k package=THT]
  R4 = Resistor [tolerance=±5% resistance=2.2k package=THT]
  D2 = Zener Diode [part_number=1N4732A breakdown_voltage=5.1V package="300 mil [THT]"]
  LED1 = LED - 5mm [color="Red (633nm)" package="5 mm [THT]"]
  T1 = Transformer [part_number="230V - 7,5 V" package="Through Hole"]
  G1 = Graetz Bridge Rectifier [package="DIP (Dual Inline) [THT]"]
  J1 = female pin header, 4 pins [form="♀ (female)"]
  Arduino_pro_mini = Arduino Pro Mini v13
  J6 = screw terminal, 6 pins
  J7 = female pin header, 4 pins [form="♀ (female)"]  # not connected
  J8 = screw terminal, 6 pins
  J5 = male pin header, 3 pins [form="♂ (male)"]

nets:
  N1: R1.Pin_0, D2.anode, G1.dc_negative, Arduino_pro_mini.GND, J5.pin1, J5.pin2
  N2: R1.Pin_1, LED1.cathode
  GND: R2.leg1, J1.pin2
  N3: R2.wiper, Arduino_pro_mini.A0
  N4: R2.leg2, J1.pin1, Arduino_pro_mini.VCC
  N5: R3.Pin_0, R4.Pin_1, D2.cathode, Arduino_pro_mini.A3
  N6: R4.Pin_0, LED1.anode, G1.dc_positive
  N7: T1.1, J6.pin1, J6.pin4
  N8: T1.3, J6.pin5, J8.pin6
  N9: T1.5, G1.ac_input_2
  N10: T1.6, G1.ac_input_1
  N11: J1.pin3, Arduino_pro_mini.A1
  N12: J1.pin4, Arduino_pro_mini.A2
  N13: Arduino_pro_mini.RAW, J5.pin3
  N14: J6.pin2, J8.pin1, J8.pin4
  N15: J6.pin3, J8.pin5
  N16: J6.pin6, J8.pin2

notes:
  to 5V DC
  2x relais brick
  + - 1 2
  - - +
  01 02 03 04 05 06 07 08 09 10 11 12 13 14 15 16 17 18
  A  B  C  D  E  F  G  H  I  J  K  L  M  N  O  P  Q  R  S  T  U  V  W  X
  +
  -
  230V continue
  230V switched on/off (light WC)
  to motor WC ventilator, switched
  to outlet trafo 230V to 5V DC
  neutral and to outlet trafo 230V to 5V DC
  to motor WC ventilator, neutral
  -   +
  no 1
  no 2
  nc 2
  nc 1
  Timer for WC ventilatormotor V1.0
  0 Watt when inactive
  18-09-2015 by hfmv

custom parts:
  Transformer: A Triad Magnetics 600Ohm:600Ohm audio transformer.
  Graetz Bridge Rectifier: Graetz Bridge Rectifier - znany także jako Mostek Graetz'a :)
  Arduino Pro Mini v13: It's blue! It's thin! It's the Arduino Pro Mini! SparkFun's minimal design approach to Arduino. This is a 5V Arduino running the 16MHz bootloader. Arduino Pro Mini does not come with connectors populated so that you can solder in any connector or wire with any orientation you need. We recommend first time Arduino users start with the Uno R3. It's a great board that will get you up and running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
